# Fritzing sketch mini-rover (saved by Fritzing 0.9.2b)
breadboards: 1

parts:
  Q1 = TRANSISTOR_NPN [package=to-92-ammo]
  Q2 = TRANSISTOR_NPN [package=to-92-ammo]
  R1 = Resistor [tolerance=±5% resistance=1k package="2512 [SMD]"]
  R2 = Resistor [tolerance=±5% resistance=1k package="2512 [SMD]"]
  D1 = Rectifier Diode [part_number=1N4001 package="300 mil [THT]"]
  D2 = Rectifier Diode [part_number=1N4001 package="300 mil [THT]"]
  BAT1 = BC9VPC [package=bc9vpc]
  M1 = DC Motor
  M2 = DC Motor
  Part1 = Arduino Uno (Rev3) - ICSP
  Part2 = HC-SR04 Ultrasonic Rangemeter

nets:
  GND: Q1.E, Q2.E, BAT1.V-, Part1.GND, Part2.GND
  N1: Q1.B, R1.Pin_0
  N2: Q1.C, D2.anode, M2.pin_1
  N3: Q2.B, R2.Pin_0
  N4: Q2.C, D1.anode, M1.pin_2
  N5: R1.Pin_1, Part1.D9_PWM
  N6: R2.Pin_1, Part1.D11_PWM/MOSI
  N7: D1.cathode, D2.cathode, BAT1.V+, M1.pin_1, M2.pin_2
  N8: Part1.D12/MISO, Part2.Trig
  N9: Part1.D13/SCK, Part2.Echo
  5V: Part1.5V, Part2.VCC
